# Fritzing sketch Schaltplan (saved by Fritzing 0.9.9b)
breadboards: 1

parts:
  R = female pin header, 6 pins [form="♀ (female)"]
  R1 = Resistor [tolerance=±5% power=0.25 resistance=10k package=THT]
  Arduino_UNO = Arduino Uno (Rev3)
  A+WV = female pin header, 6 pins [form="♀ (female)"]
  R2 = female pin header, 6 pins [form="♀ (female)"]  # not connected
  R3 = female pin header, 6 pins [form="♀ (female)"]  # not connected

nets:
  N1: R.pin3, Arduino_UNO.D5_PWM
  N2: R.pin4, Arduino_UNO.GND, A+WV.pin2, A+WV.pin4
  N3: R1.Pin_0, Arduino_UNO.A0, A+WV.pin5
  N4: R1.Pin_1, Arduino_UNO.5V
  N5: Arduino_UNO.D4, A+WV.pin3

notes:
  Rain Gauge
  Anemometer + Wind Vane
  1
  6
  RJ11 - Rain Gauge
  VCC
  GND
  RJ11 - Anemometer + Wind Vane
  VCC - Anemometer
  GND - Anemometer
  VCC - Wind Vane
  GND - Wind Vane
